// Digital circuit 10 bit teller met nand-latch reset.dig as structural Verilog
module _10_bit_teller_met_nand_latch_reset (
  input  clk,
  input  clk_2,
  input  Generator,
  input  Generator_2,
  output freq_in,
  output Q1,
  output Q2,
  output Q3,
  output Q4,
  output reset_input_2,
  output reset_input_1,
  output reset
);

  wire _4_3_p1, _8_3_p1, _7476_1_pin9, _7476_1_pin14, _7476_1_pin15, _7476_2_pin10, _7476_2_pin14,
       _7476_3_pin10, _7476_3_pin14, _7476_4_pin3, _7476_4_pin6, _7476_4_pin10, _7476_4_pin11, _7476_4_pin14,
       _7476_5_pin6, _7476_5_pin10, _7476_5_pin11, _7476_5_pin14, _7476_6_pin6, _7476_6_pin10, _7476_6_pin11,
       _7476_6_pin14, _7476_7_pin6, _7476_7_pin11, nand_2_out, nand_3_out, nand_4_out, nand_5_out,
       nand_6_out, not_1_out, not_2_out, not_3_out, not_4_out;

  _7476 _7476_1 (
    .pin1(clk_2), .pin2(1'b0), .pin3(1'b1), .pin4(1'b1), .pin5(1'b1), .pin6(1'b0), .pin7(1'b0), .pin8(1'b0),
    .pin9(_7476_1_pin9), .pin10(_7476_1_pin9), .pin11(_7476_1_pin9), .pin12(_7476_1_pin9), .pin13(1'b0),
    .pin14(_7476_1_pin14), .pin15(_7476_1_pin15), .pin16(1'b1));
  LED led_1 (.in(_7476_1_pin15));
  LED led_2 (.in(_7476_1_pin14));
  // ScopeTrigger #(.maxStepCount(50)) scopetrigger_1: pin names not known; wires that end beside it: clk
  _7476 _7476_2 (
    .pin1(clk), .pin2(1'b1), .pin3(reset), .pin4(1'b1), .pin5(1'b1), .pin6(Q1), .pin7(1'b1), .pin8(reset),
    .pin9(1'b1), .pin10(_7476_2_pin10), .pin11(Q2), .pin12(1'b1), .pin13(1'b0), .pin14(_7476_2_pin14),
    .pin15(Q1), .pin16(1'b1));
  nand nand_1 (reset, Q1, nand_2_out);
  nand nand_2 (nand_2_out, reset, nand_3_out);
  nand nand_3 (nand_3_out, Q4, Q2);
  not not_1 (not_1_out, _7476_2_pin14);
  LED _1 (.in(not_1_out));
  not not_2 (not_2_out, _7476_2_pin10);
  LED _2 (.in(not_2_out));
  not not_3 (not_3_out, _7476_3_pin14);
  LED _4 (.in(not_3_out));
  not not_4 (not_4_out, _7476_3_pin10);
  LED _8 (.in(not_4_out));
  _7476 _7476_3 (
    .pin1(Q2), .pin2(1'b1), .pin3(reset), .pin4(1'b1), .pin5(1'b1), .pin6(Q3), .pin7(1'b1), .pin8(reset),
    .pin9(1'b1), .pin10(_7476_3_pin10), .pin11(Q4), .pin12(1'b1), .pin13(1'b0), .pin14(_7476_3_pin14),
    .pin15(Q3), .pin16(1'b1));
  _7476 _7476_4 (
    .pin1(Generator_2), .pin2(1'b1), .pin3(_7476_4_pin3), .pin4(1'b1), .pin5(1'b1), .pin6(_7476_4_pin6),
    .pin7(1'b1), .pin8(_7476_4_pin3), .pin9(1'b1), .pin10(_7476_4_pin10), .pin11(_7476_4_pin11),
    .pin12(1'b1), .pin13(1'b0), .pin14(_7476_4_pin14), .pin15(_7476_4_pin6), .pin16(1'b1));
  // PolarityAwareLED _1_2: pin names not known; wires that end beside it: 1'b1, _7476_4_pin14
  // PolarityAwareLED _2_2: pin names not known; wires that end beside it: 1'b1, _7476_4_pin10
  _7476 _7476_5 (
    .pin1(_7476_4_pin11), .pin2(1'b1), .pin3(_7476_4_pin3), .pin4(1'b1), .pin5(1'b1), .pin6(_7476_5_pin6),
    .pin7(1'b1), .pin8(_7476_4_pin3), .pin9(1'b1), .pin10(_7476_5_pin10), .pin11(_7476_5_pin11),
    .pin12(1'b1), .pin13(1'b0), .pin14(_7476_5_pin14), .pin15(_7476_5_pin6), .pin16(1'b1));
  // PolarityAwareLED _4_2: pin names not known; wires that end beside it: 1'b1, _7476_5_pin14
  // PolarityAwareLED _8_2: pin names not known; wires that end beside it: 1'b1, _7476_5_pin10
  _7400 _7400_1 (
    .pin1(_7476_5_pin11), .pin2(_7476_4_pin11), .pin3(_7476_4_pin3), .pin4(1'b0), .pin5(1'b0), .pin7(1'b0),
    .pin9(1'b0), .pin10(1'b0), .pin12(1'b0), .pin13(1'b0), .pin14(1'b1));  // open: pin6, pin8, pin11
  nand nand_4 (nand_4_out, _7476_6_pin6, nand_5_out);
  _7476 _7476_6 (
    .pin1(Generator), .pin2(1'b1), .pin3(nand_4_out), .pin4(1'b1), .pin5(1'b1), .pin6(_7476_6_pin6),
    .pin7(1'b1), .pin8(nand_4_out), .pin9(1'b1), .pin10(_7476_6_pin10), .pin11(_7476_6_pin11), .pin12(1'b1),
    .pin13(1'b0), .pin14(_7476_6_pin14), .pin15(_7476_6_pin6), .pin16(1'b1));
  nand nand_5 (nand_5_out, nand_4_out, nand_6_out);
  nand nand_6 (nand_6_out, _7476_7_pin11, _7476_6_pin11);
  // PolarityAwareLED _1_3: pin names not known; wires that end beside it: _7476_6_pin14, 1'b1
  // PolarityAwareLED _2_3: pin names not known; wires that end beside it: _7476_6_pin10, 1'b1
  // PolarityAwareLED _4_3: pin names not known; wires that end beside it: _4_3_p1, 1'b1
  // PolarityAwareLED _8_3: pin names not known; wires that end beside it: _8_3_p1, 1'b1
  _7476 _7476_7 (
    .pin1(_7476_6_pin11), .pin2(1'b1), .pin3(nand_4_out), .pin4(1'b1), .pin5(1'b1), .pin6(_7476_7_pin6),
    .pin7(1'b1), .pin8(nand_4_out), .pin9(1'b1), .pin10(_8_3_p1), .pin11(_7476_7_pin11), .pin12(1'b1),
    .pin13(1'b0), .pin14(_4_3_p1), .pin15(_7476_7_pin6), .pin16(1'b1));

  assign freq_in = clk;
  assign reset_input_1 = Q2;
  assign reset_input_2 = Q4;

  // Notes on the sheet:
  //   Q1
  //   NAND-Latch
  //   RESET
  //   Q2
  //   Q4
  //   Q3
endmodule
