// Digital circuit 16 bit teller digital.dig as structural Verilog
module _16_bit_teller_digital (
  input  clk,
  input  clk_2,
  input  clk_3,
  output freq_in,
  output Q1,
  output Q2,
  output Q3,
  output Q4
);

  wire _4_p1, _8_p1, _7476_1_pin6, _7476_1_pin10, _7476_1_pin11, _7476_1_pin14, _7476_2_pin10, _7476_2_pin14,
       _7476_3_pin6, _7476_4_pin10, _7476_4_pin14, _7476_5_pin6, _7476_5_pin10, _7476_5_pin11, _7476_5_pin14,
       _7476_6_pin6, _7476_6_pin10, _7476_6_pin11, _7476_6_pin14, not_1_out, not_2_out, not_3_out, not_4_out;

  _7476 _7476_1 (
    .pin1(clk_3), .pin2(1'b1), .pin3(1'b1), .pin4(1'b1), .pin5(1'b1), .pin6(_7476_1_pin6), .pin7(1'b1),
    .pin8(1'b1), .pin9(1'b1), .pin10(_7476_1_pin10), .pin11(_7476_1_pin11), .pin12(1'b1), .pin13(1'b0),
    .pin14(_7476_1_pin14), .pin15(_7476_1_pin6), .pin16(1'b1));
  _7476 _7476_2 (
    .pin1(clk), .pin2(1'b1), .pin3(1'b1), .pin4(1'b1), .pin5(1'b1), .pin6(Q1), .pin7(1'b1), .pin8(1'b1),
    .pin9(1'b1), .pin10(_7476_2_pin10), .pin11(Q2), .pin12(1'b1), .pin13(1'b0), .pin14(_7476_2_pin14),
    .pin15(Q1), .pin16(1'b1));
  // PolarityAwareLED _1: pin names not known; wires that end beside it: _7476_1_pin14, 1'b1
  // PolarityAwareLED _2: pin names not known; wires that end beside it: _7476_1_pin10, 1'b1
  not not_1 (not_1_out, _7476_2_pin14);
  LED _1_2 (.in(not_1_out));
  // PolarityAwareLED _4: pin names not known; wires that end beside it: _4_p1, 1'b1
  not not_2 (not_2_out, _7476_2_pin10);
  LED _2_2 (.in(not_2_out));
  // PolarityAwareLED _8: pin names not known; wires that end beside it: _8_p1, 1'b1
  not not_3 (not_3_out, _7476_4_pin14);
  LED _4_2 (.in(not_3_out));
  _7476 _7476_3 (
    .pin1(_7476_1_pin11), .pin2(1'b1), .pin3(1'b1), .pin4(1'b1), .pin5(1'b1), .pin6(_7476_3_pin6),
    .pin7(1'b1), .pin8(1'b1), .pin9(1'b1), .pin10(_8_p1), .pin12(1'b1), .pin13(1'b0), .pin14(_4_p1),
    .pin15(_7476_3_pin6), .pin16(1'b1));  // open: pin11
  not not_4 (not_4_out, _7476_4_pin10);
  LED _8_2 (.in(not_4_out));
  _7476 _7476_4 (
    .pin1(Q2), .pin2(1'b1), .pin3(1'b1), .pin4(1'b1), .pin5(1'b1), .pin6(Q3), .pin7(1'b1), .pin8(1'b1),
    .pin9(1'b1), .pin10(_7476_4_pin10), .pin11(Q4), .pin12(1'b1), .pin13(1'b0), .pin14(_7476_4_pin14),
    .pin15(Q3), .pin16(1'b1));
  // ScopeTrigger scopetrigger_1: pin names not known; wires that end beside it: clk_2
  _7476 _7476_5 (
    .pin1(clk_2), .pin2(1'b1), .pin3(1'b1), .pin4(1'b1), .pin5(1'b1), .pin6(_7476_5_pin6), .pin7(1'b1),
    .pin8(1'b1), .pin9(1'b1), .pin10(_7476_5_pin10), .pin11(_7476_5_pin11), .pin12(1'b1), .pin13(1'b0),
    .pin14(_7476_5_pin14), .pin15(_7476_5_pin6), .pin16(1'b1));
  // Probe Qa on _7476_5_pin6
  // PolarityAwareLED _1_3: pin names not known; wires that end beside it: 1'b1, _7476_5_pin14
  // Probe klok on clk_2
  // Probe Qb on _7476_5_pin11
  // PolarityAwareLED _2_3: pin names not known; wires that end beside it: 1'b1, _7476_5_pin10
  // Probe Qc on _7476_6_pin6
  _7476 _7476_6 (
    .pin1(_7476_5_pin11), .pin2(1'b1), .pin3(1'b1), .pin4(1'b1), .pin5(1'b1), .pin6(_7476_6_pin6),
    .pin7(1'b1), .pin8(1'b1), .pin9(1'b1), .pin10(_7476_6_pin10), .pin11(_7476_6_pin11), .pin12(1'b1),
    .pin13(1'b0), .pin14(_7476_6_pin14), .pin15(_7476_6_pin6), .pin16(1'b1));
  // PolarityAwareLED _4_3: pin names not known; wires that end beside it: 1'b1, _7476_6_pin14
  // Probe Qd on _7476_6_pin11
  // PolarityAwareLED _8_3: pin names not known; wires that end beside it: 1'b1, _7476_6_pin10

  assign freq_in = clk;

  // Notes on the sheet:
  //   R1
  //   220 Ω
  //   R2
  //   220 Ω
  //   R3
  //   220 Ω
  //   R4
  //   220 Ω
endmodule
