// Logisim project simulatie_10_bit_teller.circ as structural Verilog: 1 circuit, main circuit main
module main (
);

  wire and_1_out, and_2_out, clock_1_out, j_k_ff_1_q, j_k_ff_1_qn, j_k_ff_2_q, j_k_ff_2_qn, j_k_ff_3_q,
       j_k_ff_3_qn, j_k_ff_4_q, j_k_ff_4_qn;

  Clock clock_1 (.out(clock_1_out));
  J_K_Flip_Flop #(.trigger("falling")) j_k_ff_1 (
    .J(1'b1), .K(1'b1), .clk(clock_1_out), .Q(j_k_ff_1_q), .Qn(j_k_ff_1_qn), .reset(and_2_out));  // open: preset
  LED #(.active("false")) led_1 (.in(j_k_ff_1_qn));
  and and_1 (and_1_out, j_k_ff_1_q, j_k_ff_2_q);
  and and_2 (and_2_out, and_1_out, j_k_ff_4_q);
  J_K_Flip_Flop #(.trigger("falling")) j_k_ff_2 (
    .J(1'b1), .K(1'b1), .clk(j_k_ff_1_q), .Q(j_k_ff_2_q), .Qn(j_k_ff_2_qn), .reset(and_2_out));  // open: preset
  LED #(.active("false")) led_2 (.in(j_k_ff_2_qn));
  J_K_Flip_Flop #(.trigger("falling")) j_k_ff_3 (
    .J(1'b1), .K(1'b1), .clk(j_k_ff_2_q), .Q(j_k_ff_3_q), .Qn(j_k_ff_3_qn), .reset(and_2_out));  // open: preset
  LED #(.active("false")) led_3 (.in(j_k_ff_3_qn));
  J_K_Flip_Flop #(.trigger("falling")) j_k_ff_4 (
    .J(1'b1), .K(1'b1), .clk(j_k_ff_3_q), .Q(j_k_ff_4_q), .Qn(j_k_ff_4_qn), .reset(and_2_out));  // open: preset
  LED #(.active("false")) led_4 (.in(j_k_ff_4_qn));
  // Digital_Oscilloscope #(.frontlines("falling"), .nState(20)) digital_oscilloscope_1: pin names not known; wires that end beside it: clock_1_out, j_k_ff_1_q, j_k_ff_2_q, j_k_ff_3_q, j_k_ff_4_q, j_k_ff_1_qn, j_k_ff_2_qn, j_k_ff_3_qn, j_k_ff_4_qn, j_k_ff_2_q, j_k_ff_4_q
endmodule
